# Fritzing sketch esquemafzz (saved by Fritzing 0.9.3b)

parts:
  Componente1 = Arduino Nano (Rev3.0)
  U1 = LM2596 step down module
  Componente2 = Arduino GSM Shield
  VCC1 = Battery
  R1 = Resistor [tolerance=±5% resistance=10k package=THT]
  S1 = Toggle Switch [package=THT]

nets:
  N1: Componente1.D3, Componente2.RST_MDM/D7
  N2: Componente1.D5, Componente2.D8
  N3: Componente1.D6, Componente2.PWM_D9
  VIN: Componente1.VIN, Componente2.5V, VCC1.+, S1.COM
  N4: Componente1.GND, U1.IN-, U1.OUT-, VCC1.-, R1.Pin_0, S1.L2
  N5: Componente1.A3, U1.OUT+, R1.Pin_1

notes:
  +12V
  -12V
  +4.5V
  -4.5V
  10k
  7.4V
  Vin

custom parts:
  LM2596 step down module: LM2596 DC-DC step down power supply module 3 A.
  Battery: Your standard 2x 18650 battery pack (7,4 Volts)
